// Logisim project simplicacao_de_circuito.Erika.circ as structural Verilog: 1 circuit, main circuit main
module main (
  input  a,
  input  b,
  input  c,
  output s1,
  output s2,
  output s3,
  output s4,
  output s5
);

  wire and_1_out, and_2_out, and_3_out, and_4_out, and_5_out, and_6_out, and_7_out, and_8_out, and_9_out,
       and_10_out, and_11_out, and_12_out, and_13_out, not_1_out, not_2_out, not_3_out, not_4_out, not_5_out,
       not_6_out, not_7_out, not_8_out, not_9_out, not_10_out, not_11_out, not_12_out, not_13_out,
       not_14_out, not_15_out, not_16_out;

  not not_1 (not_1_out, a);
  not not_2 (not_2_out, a);
  not not_3 (not_3_out, b);
  not not_4 (not_4_out, b);
  not not_5 (not_5_out, a);
  not not_6 (not_6_out, b);
  not not_7 (not_7_out, a);
  not not_8 (not_8_out, a);
  not not_9 (not_9_out, b);
  not not_10 (not_10_out, a);
  not not_11 (not_11_out, a);
  not not_12 (not_12_out, a);
  not not_13 (not_13_out, a);
  not not_14 (not_14_out, a);
  not not_15 (not_15_out, a);
  not not_16 (not_16_out, b);
  and and_1 (and_1_out, not_1_out, not_2_out);
  and and_2 (and_2_out, b, a);
  and and_3 (and_3_out, a, not_3_out);
  and and_4 (and_4_out, not_6_out, a);
  and and_5 (and_5_out, a, not_7_out);
  and and_6 (and_6_out, not_8_out, not_9_out, a);
  and and_7 (and_7_out, b, not_10_out);
  and and_8 (and_8_out, a, not_11_out);
  and and_9 (and_9_out, a, b);
  and and_10 (and_10_out, not_12_out, not_13_out);
  and and_11 (and_11_out, not_14_out, b);
  and and_12 (and_12_out, b, not_15_out);
  and and_13 (and_13_out, a, not_16_out, a);
  or or_1 (s1, and_1_out, and_2_out, and_3_out);
  or or_2 (s2, not_4_out, not_5_out);
  or or_3 (s3, and_4_out, and_5_out);
  or or_4 (s4, and_6_out, and_7_out, and_8_out, and_9_out);
  or or_5 (s5, and_10_out, and_11_out, and_12_out, and_13_out);

  assign c = a;
endmodule
